// Digital circuit hw3_d.dig as structural Verilog
module hw3_d (
  input  [3:0] Y,
  input  [3:0] X,
  input  [3:0] _5,
  input  [3:0] _6,
  input  _0,
  output [3:0] Z
);

  wire comparator_1_gt;
  wire [3:0] multiplexer_1_out;

  Comparator #(.Bits(4)) comparator_1 (.a(X), .b(Y), .gt(comparator_1_gt));  // open: eq, lt
  Multiplexer #(.Bits(4)) multiplexer_1 (.sel(comparator_1_gt), .in_0(_6), .in_1(_5), .out(multiplexer_1_out));
  Add #(.Bits(4)) add_1 (.a(multiplexer_1_out), .b(X), .c_i(_0), .s(Z));  // open: c_o

  // Notes on the sheet:
  //   _5: default 5
  //   _6: default 6
endmodule
