// Digital circuit Lec4_Mod10_Cntr.dig as structural Verilog
module Lec4_Mod10_Cntr (
  input  [1:0] Control,
  input  [3:0] D,
  input  clk,
  output [3:0] Q
);

  wire Comparator_eq;
  wire [3:0] Adder_s, multiplexer_1_out, multiplexer_2_out;

  Multiplexer #(.Bits(4), .Selector_Bits(2)) multiplexer_1 (
    .sel(Control), .in_0(Q), .in_1(multiplexer_2_out), .in_2(D), .in_3(4'b0000), .out(multiplexer_1_out));
  Register #(.Bits(4)) Register (.D(multiplexer_1_out), .C(clk), .en(1'b1), .Q(Q));
  Add #(.Bits(4)) Adder (.a(4'b0001), .b(Q), .c_i(1'b0), .s(Adder_s));  // open: c_o
  Comparator #(.Bits(4)) Comparator (.a(4'b1010), .b(Adder_s), .eq(Comparator_eq));  // open: gt, lt
  Multiplexer #(.Bits(4)) multiplexer_2 (.sel(Comparator_eq), .in_0(Adder_s), .in_1(4'b0000), .out(multiplexer_2_out));
endmodule
