// Digital circuit sync_ripple_counters.dig as structural Verilog
module sync_ripple_counters (
  input  clk,
  output [3:0] out_2,
  output [3:0] out_3,
  output [3:0] out_4,
  output [3:0] out_5
);

  wire counterpreset_1_ovf, counterpreset_2_ovf;

  CounterPreset #(.Bits(4), .maxValue(9)) counterpreset_1 (
    .en(1'b1), .C(clk), .dir(1'b0), .in(4'b0000), .ld(1'b0), .clr(1'b0), .out(out_2),
    .ovf(counterpreset_1_ovf));
  CounterPreset #(.Bits(4), .maxValue(9)) counterpreset_2 (
    .en(1'b1), .C(clk), .dir(1'b0), .in(4'b0000), .ld(1'b0), .clr(1'b0), .out(out_4),
    .ovf(counterpreset_2_ovf));
  CounterPreset #(.Bits(4), .maxValue(9)) counterpreset_3 (
    .en(1'b1), .C(counterpreset_1_ovf), .dir(1'b0), .in(4'b0000), .ld(1'b0), .clr(1'b0), .out(out_3));  // open: ovf
  CounterPreset #(.Bits(4), .maxValue(9)) counterpreset_4 (
    .en(counterpreset_2_ovf), .C(clk), .dir(1'b0), .in(4'b0000), .ld(1'b0), .clr(1'b0), .out(out_5));  // open: ovf

  // Notes on the sheet:
  //   Ripple Counter
  //   Synchronous Counter
endmodule
